# Fritzing sketch capture_point (saved by Fritzing 0.9.3b)
breadboards: 1

parts:
  Grove1 = Grove 4 Digit Display
  Часть1 = Arduino Nano (Rev3.0)
  S1 = Pushbutton [package="[THT]"]
  S2 = Pushbutton [package="[THT]"]
  S3 = Pushbutton [package="[THT]"]
  R1 = Resistor [tolerance=±5% resistance=10k package=THT]
  R2 = Resistor [tolerance=±5% resistance=10k package=THT]
  R3 = Resistor [tolerance=±5% resistance=10k package=THT]
  BAT1 = BC9VPC [package=bc9vpc]
  J1 = Piezo Speaker
  R4 = Resistor [tolerance=±5% resistance=100 package=THT]

nets:
  GND: Grove1.GND, Часть1.GND, R1.Pin_1, R2.Pin_1, R3.Pin_1, BAT1.V-, J1.pin1
  VCC: Grove1.VCC, Часть1.5V, S1.Pin_3, S1.Pin_4, S2.Pin_3, S2.Pin_4, S3.Pin_3, S3.Pin_4
  N1: Grove1.DIO, Часть1.D4
  N2: Grove1.CLK, Часть1.D5
  N3: Часть1.D8, R4.Pin_1
  N4: Часть1.D10, S3.Pin_1, S3.Pin_2, R3.Pin_0
  N5: Часть1.D11/MOSI, S2.Pin_1, S2.Pin_2, R2.Pin_0
  N6: Часть1.D12/MISO, S1.Pin_1, S1.Pin_2, R1.Pin_0
  N7: Часть1.VIN, BAT1.V+
  N8: J1.pin2, R4.Pin_0
